# Fritzing sketch alexa lift (saved by Fritzing 0.9.3b)
breadboards: 2

parts:
  mega = Arduino Mega 2560 (Rev3)
  Raspberry_Pi_1 = Raspberry Pi 3 [part_number=RPI-3-V1.2]  # not connected
  S1 = SWITCH-DPDT [package=ms]
  hc-sr1 = hc-sr04  # not connected
  7_Segment1 = 7 Segment Display
  U2 = NodeMCU V3.0
  S2 = H-Bridge with L298N
  M1 = Stepper Motor - Bipolar
  LED11 = LED - 3mm [color="Red (633nm)" package="3 mm [THT]"]
  LED12 = LED - 3mm [color="Red (633nm)" package="3 mm [THT]"]
  LED13 = LED - 3mm [color="Red (633nm)" package="3 mm [THT]"]
  LED14 = LED - 3mm [color="Red (633nm)" package="3 mm [THT]"]
  LED15 = LED - 3mm [color="Red (633nm)" package="3 mm [THT]"]
  LED16 = LED - 3mm [color="Red (633nm)" package="3 mm [THT]"]
  R1 = Resistor [tolerance=±5% resistance=220 package="1206 [SMD]"]
  R2 = Resistor [tolerance=±5% resistance=220 package="1206 [SMD]"]
  R3 = Resistor [tolerance=±5% resistance=220 package="1206 [SMD]"]
  R4 = Resistor [tolerance=±5% resistance=220 package="1206 [SMD]"]
  R5 = Resistor [tolerance=±5% resistance=220 package="1206 [SMD]"]
  R6 = Resistor [tolerance=±5% resistance=220 package="1206 [SMD]"]
  J5 = Power Jack [package=power_jack_slot]
  J6 = female pin header, 2 pins [form="♀ (female)"]
  BAT2 = BC9VPC [package=bc9vpc]
  KY-1 = Keyes Relay [package=THT]
  LED17 = LED - 5mm [color="Red (633nm)" package="5 mm [THT]"]
  BATT1 = LiPoly Battery (1300mAh)
  J7 = Power Jack [package=power_jack_slot]

nets:
  N1: mega.D18/TX1, KY-1.signal
  GND: mega.GND, 7_Segment1.common_cathode, U2.GND, U2.Vin
  N2: mega.5V, S1.5
  N3: mega.D2_PWM, U2.D0, LED11.anode
  N4: mega.D3_PWM, U2.D5, LED16.anode
  N5: mega.D4_PWM, U2.D4, LED15.anode
  N6: mega.D5_PWM, U2.D3, LED14.anode
  N7: mega.D6_PWM, U2.D2, LED13.anode
  N8: mega.D7_PWM, LED12.anode
  N9: mega.D23, S2.ENA
  N10: mega.D24, S1.4
  N11: mega.D25, S2.IN1
  N12: mega.D27, S2.IN2
  N13: mega.D29, S2.IN3
  N14: mega.D31, S2.IN4
  N15: mega.D33, S2.ENB
  N16: mega.D35, 7_Segment1.Segment_E
  N17: mega.D37, 7_Segment1.Segment_D
  N18: mega.D41, 7_Segment1.Segment_C
  N19: mega.D43, 7_Segment1.Segment_DP
  N20: mega.D45, 7_Segment1.Segment_B
  N21: mega.D47, 7_Segment1.Segment_A
  N22: mega.D49, 7_Segment1.Segment_F
  N23: mega.D51, 7_Segment1.Segment_G
  N24: U2.D1, LED12.cathode, R5.Pin_0
  N25: S2.12V, J7.PWR
  N26: S2.M1-01, M1.A
  N27: S2.M1-02, M1.C
  N28: S2.M2-01, M1.B
  N29: S2.M2-02, M1.D
  N30: LED11.cathode, R6.Pin_0
  N31: LED13.cathode, R4.Pin_0
  N32: LED14.cathode, R3.Pin_0
  N33: R1.Pin_1, R2.Pin_1, R3.Pin_1, R4.Pin_1, R5.Pin_1, R6.Pin_1
  N34: J5.GND, J5.tip_GND, J6.pin1, BAT2.V-
  N35: J5.PWR, J5.tip_PWR, J5.GNDBREAK, J6.pin2, BAT2.V+
  N36: KY-1.NC, LED17.anode
  N37: LED17.cathode, BATT1.negative

custom parts:
  NodeMCU V3.0: ESP8266 based NodeMCU
  H-Bridge with L298N: h-bridge
  Power Jack: Power Jack This is the standard 5.5mm barrel jack for power. Ths one is modified to mate with the barrel plug part and allow the two to "connect" so batteries and wall warts can be "connected" in breadboard and will go through to schematic.
  Keyes Relay: The Keyes 5V relay module is suitable for SCM development, home appliance control. It uses a 5V~12V TIL control signal which can control DC / AC signal.
  LiPoly Battery (1300mAh): Lithium Ion Polymer Battery (1300mAh)
